// Logisim project PROYECTO_grupo3.circ as structural Verilog: 21 circuits, main circuit contador_FSM
module contador_FSM (
  input  Clk,
  input  Clear,
  output Q3,
  output Q2,
  output Q1,
  output Q0
);

  wire circuito_q0_1_out_2, circuito_q1_1_s, circuito_q2_1_s2, circuito_q3_1_s3;

  CIRCUITO_Q2 circuito_q2_1 (.q3(Q3), .q2(Q2), .q1(Q1), .q0(Q0), .S2(circuito_q2_1_s2));
  CIRCUITO_Q3 circuito_q3_1 (.q3(Q3), .q2(Q2), .q1(Q1), .q0(Q0), .S3(circuito_q3_1_s3));
  CIRCUITO_Q1 circuito_q1_1 (.q3(Q3), .q2(Q2), .q1(Q1), .q0(Q0), .S(circuito_q1_1_s));
  CIRCUITO_Q0 circuito_q0_1 (.q0(Q0), .out_2(circuito_q0_1_out_2));
  D_Flip_Flop d_ff_1 (.D(circuito_q1_1_s), .clk(Clk), .Q(Q1), .reset(Clear));  // open: Qn, preset
  D_Flip_Flop d_ff_2 (.D(circuito_q0_1_out_2), .clk(Clk), .Q(Q0), .reset(Clear));  // open: Qn, preset
  D_Flip_Flop d_ff_3 (.D(circuito_q3_1_s3), .clk(Clk), .Q(Q3), .reset(Clear));  // open: Qn, preset
  D_Flip_Flop d_ff_4 (.D(circuito_q2_1_s2), .clk(Clk), .Q(Q2), .reset(Clear));  // open: Qn, preset
endmodule

module CIRCUITO_Q3 (
  input  q3,
  input  q2,
  input  q1,
  input  q0,
  output S3
);

  wire and_1_out, and_2_out, and_3_out, and_4_out, not_1_out, not_2_out;

  not not_1 (not_1_out, q2);
  not not_2 (not_2_out, q0);
  and and_1 (and_1_out, q2, q1);
  and and_2 (and_2_out, q3, not_2_out, q2);
  and and_3 (and_3_out, q3, not_1_out, q0);
  and and_4 (and_4_out, q3, q1);
  or or_1 (S3, and_1_out, and_2_out, and_3_out, and_4_out);
endmodule

module CIRCUITO_Q2 (
  input  q3,
  input  q2,
  input  q1,
  input  q0,
  output S2
);

  wire and_1_out, and_2_out, and_3_out, and_4_out, and_5_out, not_1_out, not_2_out, not_3_out, not_4_out;

  not not_1 (not_1_out, q3);
  not not_2 (not_2_out, q2);
  not not_3 (not_3_out, q1);
  not not_4 (not_4_out, q0);
  and and_1 (and_1_out, q3, q2, q1, q0);
  and and_2 (and_2_out, q2, not_3_out, not_4_out);
  and and_3 (and_3_out, q3, not_2_out, not_4_out);
  and and_4 (and_4_out, not_1_out, not_2_out, q0);
  and and_5 (and_5_out, q3, not_2_out, not_3_out);
  or or_1 (S2, and_1_out, and_2_out, and_3_out, and_4_out, and_5_out);
endmodule

module CIRCUITO_Q1 (
  input  q3,
  input  q2,
  input  q1,
  input  q0,
  output S
);

  wire and_1_out, and_2_out, and_3_out, and_4_out, and_5_out, not_1_out, not_2_out, not_3_out;

  not not_1 (not_1_out, q3);
  not not_2 (not_2_out, q1);
  not not_3 (not_3_out, q0);
  and and_1 (and_1_out, not_1_out, not_2_out, not_3_out);
  and and_2 (and_2_out, not_1_out, q1, q0);
  and and_3 (and_3_out, not_1_out, q2, not_2_out);
  and and_4 (and_4_out, q3, q2, not_3_out);
  and and_5 (and_5_out, q3, q2, q1);
  or or_1 (S, and_1_out, and_2_out, and_3_out, and_4_out, and_5_out);
endmodule

module CIRCUITO_Q0 (
  input  q0,
  output out_2
);

  not not_1 (out_2, q0);
endmodule

module contador_FSM_test (
  input  Clear
);

  wire Clk_out;
  wire [3:0] binary_to_bcd_converter_1_p2, binary_to_bcd_converter_1_p3, contador_fsm_1_q0;

  Clock Clk (.out(Clk_out));
  contador_FSM contador_fsm_1 (
    .Clk(Clk_out), .Clear(Clear), .Q3(contador_fsm_1_q0[3]), .Q2(contador_fsm_1_q0[2]),
    .Q1(contador_fsm_1_q0[1]), .Q0(contador_fsm_1_q0[0]));
  Hex_Digit_Display hex_digit_display_1 (.value(binary_to_bcd_converter_1_p2));  // open: dp
  // Binary_to_BCD_converter #(.binvalue(4)) binary_to_bcd_converter_1: pin names not known; wires that end beside it: contador_fsm_1_q0, binary_to_bcd_converter_1_p2, binary_to_bcd_converter_1_p3
  Hex_Digit_Display hex_digit_display_2 (.value(binary_to_bcd_converter_1_p3));  // open: dp
endmodule

module circ_q3 (
  input  E3,
  input  E2,
  input  E1,
  input  E0,
  output Q3
);

  wire and_1_out, and_2_out, and_3_out, and_4_out, not_1_out, not_2_out, not_3_out, not_4_out;

  not not_1 (not_1_out, E3);
  not not_2 (not_2_out, E2);
  not not_3 (not_3_out, E1);
  not not_4 (not_4_out, E0);
  and and_1 (and_1_out, not_1_out, E1, E0);
  and and_2 (and_2_out, not_1_out, E2);
  and and_3 (and_3_out, E2, E1);
  and and_4 (and_4_out, E3, not_2_out, not_3_out, not_4_out);
  or or_1 (Q3, and_4_out, and_1_out, and_2_out, and_3_out);
endmodule

module circ_q2 (
  input  E3,
  input  E2,
  input  E1,
  input  E0,
  output Q2
);

  wire and_1_out, and_2_out, and_3_out, and_4_out, not_1_out, not_2_out, not_3_out;

  not not_1 (not_1_out, E3);
  not not_2 (not_2_out, E1);
  not not_3 (not_3_out, E0);
  and and_1 (and_1_out, not_1_out, E1, not_3_out);
  and and_2 (and_2_out, E3, E2, E0);
  and and_3 (and_3_out, E2, not_2_out);
  and and_4 (and_4_out, E3, not_2_out, E0);
  or or_1 (Q2, and_1_out, and_2_out, and_3_out, and_4_out);
endmodule

module circ_q1 (
  input  E3,
  input  E2,
  input  E1,
  input  E0,
  output Q1
);

  wire and_1_out, and_2_out, and_3_out, and_4_out, not_1_out, not_2_out, not_3_out;

  not not_1 (not_1_out, E3);
  not not_2 (not_2_out, E1);
  not not_3 (not_3_out, E0);
  and and_1 (and_1_out, not_1_out, not_2_out, E0);
  and and_2 (and_2_out, E1, not_3_out);
  and and_3 (and_3_out, E2, not_2_out, E0);
  and and_4 (and_4_out, not_1_out, E2, E1);
  or or_1 (Q1, and_1_out, and_2_out, and_3_out, and_4_out);
endmodule

module circ_q0 (
  input  E0,
  output Q0
);


  assign Q0 = E0;
endmodule

module contador_opt (
  input  Reset,
  input  Clk,
  output Q3,
  output Q2,
  output Q1,
  output [3:0] out_6,
  output Q0
);

  wire tq0, tq1, tq2, tq3;

  Counter #(.max('hf), .width(4)) counter_1 (
    .clr(Reset), .load(1'b0), .up(1'b1), .count(1'b1), .clk(Clk), .Q({tq3, tq2, tq1, tq0}));  // open: D, carry
  circ_q3 circ_q3_1 (.E3(tq3), .E2(tq2), .E1(tq1), .E0(tq0), .Q3(out_6[3]));
  circ_q2 circ_q2_1 (.E3(tq3), .E2(tq2), .E1(tq1), .E0(tq0), .Q2(out_6[2]));
  circ_q1 circ_q1_1 (.E3(tq3), .E2(tq2), .E1(tq1), .E0(tq0), .Q1(out_6[1]));
  circ_q0 circ_q0_1 (.E0(tq0), .Q0(out_6[0]));

  assign Q0 = out_6[0];
  assign Q1 = out_6[1];
  assign Q2 = out_6[2];
  assign Q3 = out_6[3];
endmodule

module contador_opt_test (
  input  Reset
);

  wire Clk_out;
  wire [3:0] binary_to_bcd_converter_1_p1, binary_to_bcd_converter_1_p3, binary_to_bcd_converter_1_p4;

  Clock Clk (.out(Clk_out));
  contador_opt contador_opt_1 (
    .Reset(Reset), .Clk(Clk_out), .Q3(binary_to_bcd_converter_1_p1[3]), .Q1(binary_to_bcd_converter_1_p1[2]),
    .Q0(binary_to_bcd_converter_1_p1[1]));  // open: Q2, out_6
  Hex_Digit_Display hex_digit_display_1 (.value(binary_to_bcd_converter_1_p3));  // open: dp
  // Binary_to_BCD_converter #(.binvalue(4)) binary_to_bcd_converter_1: pin names not known; wires that end beside it: binary_to_bcd_converter_1_p1[0], binary_to_bcd_converter_1_p1, binary_to_bcd_converter_1_p3, binary_to_bcd_converter_1_p4
  Hex_Digit_Display hex_digit_display_2 (.value(binary_to_bcd_converter_1_p4));  // open: dp
endmodule

module transcod_puertas (
  input  X0,
  input  X1,
  input  X2,
  input  X3,
  output A,
  output B,
  output C,
  output D,
  output E,
  output F,
  output G
);

  wire and_1_out, and_2_out, and_3_out, and_4_out, and_5_out, and_6_out, and_7_out, and_8_out, and_9_out,
       and_10_out, and_11_out, and_12_out, and_13_out, and_14_out, and_15_out, and_16_out, and_17_out,
       and_18_out, and_19_out, and_20_out, and_21_out, and_22_out, and_23_out, and_24_out, and_25_out,
       and_26_out, and_27_out, and_28_out, and_29_out, and_30_out, and_31_out, and_32_out, and_33_out,
       and_34_out, and_35_out, tnX0, tnX1, tnX2, tnX3;

  and and_1 (and_1_out, tnX3, X1);
  and and_2 (and_2_out, tnX3, X2, X0);
  and and_3 (and_3_out, X2, X1);
  and and_4 (and_4_out, X3, tnX0);
  and and_5 (and_5_out, tnX1, X0);
  and and_6 (and_6_out, tnX3, X2);
  and and_7 (and_7_out, X3, tnX2);
  and and_8 (and_8_out, tnX3, tnX1);
  and and_9 (and_9_out, tnX3, X0);
  and and_10 (and_10_out, tnX2, tnX0);
  and and_11 (and_11_out, X1, tnX0);
  and and_12 (and_12_out, X3, X1);
  and and_13 (and_13_out, X3, X2);
  and and_14 (and_14_out, tnX2, X1);
  and and_15 (and_15_out, X3, tnX2);
  and and_16 (and_16_out, X3, X0);
  and and_17 (and_17_out, X1, tnX0);
  and and_18 (and_18_out, tnX3, X2, tnX1);
  and and_19 (and_19_out, tnX2, tnX0);
  and and_20 (and_20_out, X3, tnX2, tnX1);
  or or_1 (A, and_19_out, and_1_out, and_2_out, and_3_out, and_4_out, and_20_out);
  or or_2 (C, and_5_out, and_6_out, and_7_out, and_8_out, and_9_out);
  or or_3 (E, and_10_out, and_11_out, and_12_out, and_13_out);
  or or_4 (G, and_14_out, and_15_out, and_16_out, and_17_out, and_18_out);
  and and_21 (and_21_out, X2, tnX1, X0);
  and and_22 (and_22_out, tnX2, X1, X0);
  and and_23 (and_23_out, X2, X1, tnX0);
  and and_24 (and_24_out, X3, tnX1);
  and and_25 (and_25_out, tnX3, tnX2, tnX0);
  or or_5 (D, and_21_out, and_22_out, and_23_out, and_24_out, and_25_out);
  and and_26 (and_26_out, X3, tnX1, X0);
  and and_27 (and_27_out, tnX2, tnX0);
  and and_28 (and_28_out, tnX3, tnX1, tnX0);
  and and_29 (and_29_out, tnX3, X1, X0);
  and and_30 (and_30_out, tnX3, tnX2);
  and and_31 (and_31_out, tnX1, tnX0);
  and and_32 (and_32_out, X2, tnX0);
  and and_33 (and_33_out, tnX3, X2, tnX1);
  and and_34 (and_34_out, X3, tnX2);
  and and_35 (and_35_out, X3, X1);
  or or_6 (B, and_26_out, and_27_out, and_28_out, and_29_out, and_30_out);
  or or_7 (F, and_31_out, and_32_out, and_33_out, and_34_out, and_35_out);
  not not_1 (tnX0, X0);
  not not_2 (tnX1, X1);
  not not_3 (tnX2, X2);
  not not_4 (tnX3, X3);

  // Other names for the same wires on the sheet: tX0 = X0; tX1 = X1; tX2 = X2; tX3 = X3
endmodule

module transcod_puertas_test (
  input  [3:0] InputBinary
);

  wire tA, tB, tC, tD, tE, tF, tG;

  _7_Segment_Display u_7_segment_display_1 (.g(tG), .f(tF), .a(tA), .b(tB), .e(tE), .d(tD), .c(tC));  // open: dp
  transcod_puertas transcod_puertas_1 (
    .X0(InputBinary[0]), .X1(InputBinary[1]), .X2(InputBinary[2]), .X3(InputBinary[3]), .A(tA), .B(tB),
    .C(tC), .D(tD), .E(tE), .F(tF), .G(tG));
endmodule

module transcod_PLA (
  input  [3:0] Entrada,
  output [6:0] Salida
);

  // PlaRom #(.Contents("1*7 2 1 1 2 1*3 2 2 1 2 1*3 2 1 2 1 2 2 1 1 2*4 1*3 2 1 1 2 2 1 2 1 2 1 2*4 1 1 2 2 1 2*4 1 2*4 1*6 0 0 1 1 0*4 1 1 0 1 1 0 1*5 0 0 1 0 1 1 0 0 1*3 0 1 1 0 1 1 0 0 1*8 0*4 1*10 0 0 1*5 0 1*3 0 0 1*6 0 0 1*3 0 0 1*4 0 1 1 0 0 1*5 0*3 1*3"), .\and (16), .outputs(7)) plarom_1: pin names not known; wires that end beside it: Entrada, Salida
endmodule

module transcod_PLA_test (
  input  [3:0] Entrada
);

  wire tA, tB, tC, tD, tE, tF, tG;

  transcod_PLA transcod_pla_1 (.Entrada(Entrada), .Salida({tA, tB, tC, tD, tE, tF, tG}));
  _7_Segment_Display u_7_segment_display_1 (.g(tG), .f(tF), .a(tA), .b(tB), .e(tE), .d(tD), .c(tC));  // open: dp
endmodule

module circuito_final (
  input  CLK,
  input  Clear
);

  wire tAf, tBf, tCf, tDf, tEf, tFf, tGf;
  wire [3:0] contador_fsm_1_q3;

  contador_FSM contador_fsm_1 (
    .Clk(CLK), .Clear(Clear), .Q3(contador_fsm_1_q3[0]), .Q2(contador_fsm_1_q3[1]),
    .Q1(contador_fsm_1_q3[2]), .Q0(contador_fsm_1_q3[3]));
  _7_Segment_Display u_7_segment_display_1 (.g(tGf), .f(tFf), .a(tAf), .b(tBf), .e(tEf), .d(tDf), .c(tCf));  // open: dp
  transcod_PLA transcod_pla_1 (.Entrada(contador_fsm_1_q3), .Salida({tAf, tBf, tCf, tDf, tEf, tFf, tGf}));
endmodule

module transcod_ROM (
  input  [3:0] Entrada,
  output x,
  output A,
  output B,
  output C,
  output D,
  output E,
  output F,
  output G
);

  ROM #(.addrWidth(4)) rom_1 (.addr(Entrada), .data({x, A, B, C, D, E, F, G}));

  // Notes on the sheet:
  //   contents of rom_1 (hex, n*v repeats v):
  //   7e 30 6d 79 33 5b 5f 70 7f 7b 77 1f 4e 3d 4f 47
endmodule

module transcod_ROM_test (
  input  [3:0] Entrada
);

  wire A, B, C, D, E, F, G;

  _7_Segment_Display u_7_segment_display_1 (.g(G), .f(F), .a(A), .b(B), .e(E), .d(D), .c(C));  // open: dp
  transcod_ROM transcod_rom_1 (.Entrada(Entrada), .A(A), .B(B), .C(C), .D(D), .E(E), .F(F), .G(G));  // open: x
endmodule

module transcod_deco (
  input  Enable,
  input  x0,
  input  x1,
  input  x2,
  input  x3,
  output A,
  output B,
  output C,
  output D,
  output E,
  output F,
  output G
);

  wire deco0, deco1, deco2, deco3, deco4, deco5, deco6, deco7, deco8, deco9, decoA, decoB, decoC, decoD,
       decoE, decoF;

  Decoder #(.select(4)) decoder_1 (
    .out0(deco0), .out1(deco1), .out2(deco2), .out3(deco3), .out4(deco4), .out5(deco5), .out6(deco6),
    .out7(deco7), .out8(deco8), .out9(deco9), .out10(decoA), .out11(decoB), .out12(decoC), .out13(decoD),
    .out14(decoE), .out15(decoF), .sel({x3, x2, x1, x0}), .en(Enable));
  or or_1 (E, deco0, deco2, deco6, deco8, decoA, decoB, decoC, decoD, decoE, decoF);
  or or_2 (G, deco2, deco3, deco4, deco5, deco6, deco8, deco9, decoA, decoB, decoD, decoE, decoF);
  or or_3 (B, deco0, deco1, deco2, deco3, deco4, deco7, deco8, deco9, decoA, decoD);
  or or_4 (D, deco0, deco2, deco3, deco5, deco6, deco8, deco9, decoB, decoC, decoD, decoE);
  or or_5 (F, deco0, deco4, deco5, deco6, deco8, deco9, decoA, decoB, decoC, decoE, decoF);
  or or_6 (A, deco0, deco2, deco3, deco5, deco6, deco7, deco8, deco9, decoA, decoC, decoE, decoF);
  or or_7 (C, deco0, deco1, deco3, deco4, deco5, deco6, deco7, deco8, deco9, decoA, decoB, decoD);
endmodule

module transcod_deco_test (
  input  Enable,
  input  [3:0] Entrada
);

  wire A, B, C, D, E, F, G;

  _7_Segment_Display u_7_segment_display_1 (.g(G), .f(F), .a(A), .b(B), .e(E), .d(D), .c(C));  // open: dp
  transcod_deco transcod_deco_1 (
    .Enable(Enable), .x0(Entrada[0]), .x1(Entrada[1]), .x2(Entrada[2]), .x3(Entrada[3]), .A(A), .B(B), .C(C),
    .D(D), .E(E), .F(F), .G(G));
endmodule
